# Fritzing sketch robot_minisonar (saved by Fritzing 0.9.0b)
breadboards: 1

parts:
  Part1 = Arduino Pro Mini v13
  M1 = DC Motor
  M2 = DC Motor
  LED1 = LED - 5mm [color="Red (633nm)" package="5 mm [THT]"]
  J1 = Piezo Speaker
  U4 = MLX90614 [package=to-39]
  U5 = MLX90614 [package=to-39]
  VCC2 = Battery  # not connected
  U1 = SWITCH_SPDT [package=kps-1290]
  IC1 = L293D [package=THT]
  VCC1 = Battery
  R1 = Resistor [tolerance=±5% resistance=470 package=THT]

nets:
  N1: Part1.VCC, U5.PWM_SDA, U1.S, IC1.Enable_1, IC1.+Vmotor, IC1.Enable_2, IC1.+V
  N2: Part1.GND, J1.pin1, U5.SCL_VZ, IC1.0V, VCC1.-, R1.Pin_1
  N3: Part1.D12/MISO, U4.SCL_VZ
  N4: Part1.D11_PWM/MOSI, U4.PWM_SDA
  N5: Part1.D10_PWM/SS, J1.pin2
  N6: Part1.D8, LED1.anode
  N7: Part1.D7, IC1.In_3
  N8: Part1.D6_PWM, IC1.In_4
  N9: Part1.D5_PWM, IC1.In_1
  N10: Part1.D4, IC1.In_2
  N11: M1.pin_1, IC1.Out_4_(_Controlled_by_Enable_2_)
  N12: M1.pin_2, IC1.Out_3_(_Controlled_by_Enable_2_)
  N13: M2.pin_1, IC1.Out_1_(_Controlled_by_Enable_1_)
  N14: M2.pin_2, IC1.Out_2_(_Controlled_by_Enable_1_)

notes:
  http://blog.mshams.ir
  Mini sonar robot
